# Fritzing sketch microboard_atmega (saved by Fritzing 0.8.3b)
circuit board: 3.92cm x 5cm
breadboards: 1

parts:
  IC1 = ATMega8 [package=DIL]
  GEN_SLOT = male pin header, 11 pins [form="♂ (male)"]
  SPI_SLOT = male pin header, 11 pins [form="♂ (male)"]
  IC2 = FTDI [package=SIL]
  R1 = Resistor [tolerance=±5% resistance=10k package=THT]
  PWR = male pin header, 2 pins [form="♂ (male)"]
  RESET = male pin header, 2 pins [form="♂ (male)"]
  R2 = Resistor [tolerance=±5% resistance=2.2k package=THT]
  R3 = Resistor [tolerance=±5% resistance=2.2k package=THT]

nets:
  N1: IC1.RESET/PC6, R1.Pin_1, RESET.pin2
  N2: IC1.Rx/PD0, IC2.RX
  N3: IC1.Tx/PD1, IC2.TX
  N4: IC1.INT0/PD2, GEN_SLOT.pin3
  N5: IC1.INT1/PD3, SPI_SLOT.pin11
  N6: IC1.XCK/T0/PD4, SPI_SLOT.pin10
  VCC: IC1.VCC, IC1.AVCC, IC1.AREF, GEN_SLOT.pin2, SPI_SLOT.pin2, R1.Pin_0, PWR.pin2, R2.Pin_0, R3.Pin_0
  GND: IC1.GND, GEN_SLOT.pin1, SPI_SLOT.pin1, IC2.GND/Black, PWR.pin1, RESET.pin1
  N7: IC1.T1/PD5, SPI_SLOT.pin9
  N8: IC1.AIN0/PD6, SPI_SLOT.pin8
  N9: IC1.AIN1/PD7, SPI_SLOT.pin7
  N10: IC1.ICP1/PB0, SPI_SLOT.pin6
  N11: IC1.OC1A/PB1, GEN_SLOT.pin10
  N12: IC1.OC1B/SS/PB2, GEN_SLOT.pin7
  N13: IC1.MOSI/OC2/PB3, SPI_SLOT.pin4
  N14: IC1.MISO/PB4, SPI_SLOT.pin5
  N15: IC1.SCK/PB5, SPI_SLOT.pin3
  N16: IC1.ADC0/PC0, GEN_SLOT.pin11
  N17: IC1.ADC1/PC1, GEN_SLOT.pin9
  N18: IC1.ADC2/PC2, GEN_SLOT.pin8
  N19: IC1.ADC3/PC3, GEN_SLOT.pin6
  N20: IC1.ADC4/SDA/PC4, GEN_SLOT.pin4, R3.Pin_1
  N21: IC1.ADC5/SCL/PC5, GEN_SLOT.pin5, R2.Pin_1

notes:
  http://thegaragelab.com
  Babyduino Mk2
  +
  -
  Microboard, Microboard ATmega, 2B
