# Fritzing sketch microboard_attiny (saved by Fritzing 0.8.5b)
circuit board: 1.6cm x 2.8cm
breadboards: 1

parts:
  BC547 = NPN-Transistor [package="TO92 [THT]"]
  U1 = attiny85 [package=dip]
  R1 = Resistor [tolerance=±5% resistance=10k package=THT]
  D1 = Rectifier Diode [part_number=1N4001 package="300 mil [THT]"]
  J1 = male pin header, 4 pins [form="♂ (male)"]
  J2 = male pin header, 4 pins [form="♂ (male)"]
  SERIAL = male pin header, 6 pins [form="♂ (male)"]
  LOAD = male pin header, 2 pins [form="♂ (male)"]

nets:
  DATA: BC547.E, U1.Pin_1, D1.anode, J1.pin1
  N1: BC547.B, R1.Pin_1
  RX: BC547.C, SERIAL.pin4
  N2: U1.Pin_2, J1.pin2, LOAD.pin2
  N3: U1.Pin_3, J1.pin3
  GND: U1.Pin_4, J1.pin4, SERIAL.pin1, LOAD.pin1
  N4: U1.Pin_5, J2.pin4
  N5: U1.Pin_6, J2.pin3
  N6: U1.Pin_7, J2.pin2
  N7: U1.Pin_8, J2.pin1
  TX: R1.Pin_0, D1.cathode, SERIAL.pin5

notes:
  Microboard, ATtiny Breakout Board, 1A
  ATtiny
  GND
