# Fritzing sketch baseboard (saved by Fritzing 0.8.7b)
circuit board: 12cm x 5.5cm
breadboards: 1

parts:
  IC1 = Microboard [package=MB]
  SPI2_X1 = female pin header, 2 pins [form="♀ (female)"]
  SPI1_X1 = female pin header, 2 pins [form="♀ (female)"]
  SPI0_X1 = female pin header, 2 pins [form="♀ (female)"]
  SPI2 = female pin header, 5 pins [form="♀ (female)"]
  SPI1 = female pin header, 5 pins [form="♀ (female)"]
  SPI0 = female pin header, 5 pins [form="♀ (female)"]
  SLOT2 = female pin header, 5 pins [form="♀ (female)"]
  SLOT1 = female pin header, 5 pins [form="♀ (female)"]
  SLOT0 = female pin header, 5 pins [form="♀ (female)"]
  Pad1 = Pad [width=28.3675666666667 height=25.9324968888889 connect=center]

nets:
  N1: IC1.EX2, SPI2_X1.pin2
  N2: IC1.EN2, SPI2_X1.pin1
  N3: IC1.EX1, SPI1_X1.pin2
  N4: IC1.EN1, SPI1_X1.pin1
  N5: IC1.EX0, SPI0_X1.pin2
  N6: IC1.EN0, SPI0_X1.pin1
  N7: IC1.MISO, SPI2.pin5, SPI1.pin5, SPI0.pin5
  N8: IC1.MOSI, SPI2.pin4, SPI1.pin4, SPI0.pin4
  N9: IC1.SCK, SPI2.pin3, SPI1.pin3, SPI0.pin3
  N10: IC1.VCC#10, SPI2.pin2, SPI1.pin2, SPI0.pin2
  GND: IC1.GND, SPI2.pin1, SPI1.pin1, SPI0.pin1, SLOT2.pin1, SLOT1.pin1, SLOT0.pin1, Pad1.pad
  N11: IC1.S2OUT, SLOT2.pin5
  N12: IC1.S2IN, SLOT2.pin4
  N13: IC1.S2EX, SLOT2.pin3
  N14: IC1.S1OUT, SLOT1.pin5
  N15: IC1.S1IN, SLOT1.pin4
  N16: IC1.S1EX, SLOT1.pin3
  N17: IC1.S0OUT, SLOT0.pin5
  N18: IC1.S0IN, SLOT0.pin4
  N19: IC1.S0EX, SLOT0.pin3
  N20: IC1.VCC#21, SLOT2.pin2, SLOT1.pin2, SLOT0.pin2

notes:
  Microboard IO Dock
  http://thegaragelab.com/
  I2C
