# Fritzing sketch lpc1114_adaptor (saved by Fritzing 0.8.7b)
circuit board: 2cm x 3.8cm
breadboards: 1

parts:
  IC1 = DIP28 [package=DILW]
  IC2 = DIP28 [package=DIL]

nets:
  N1: IC1.1, IC2.1
  N2: IC1.2, IC2.2
  N3: IC1.3, IC2.3
  N4: IC1.4, IC2.4
  N5: IC1.5, IC2.5
  N6: IC1.6, IC2.6
  N7: IC1.7, IC2.7
  N8: IC1.8, IC2.8
  N9: IC1.9, IC2.9
  N10: IC1.10, IC2.10
  N11: IC1.11, IC2.11
  N12: IC1.12, IC2.12
  N13: IC1.13, IC2.13
  N14: IC1.14, IC2.14
  N15: IC1.15, IC2.15
  N16: IC1.16, IC2.16
  N17: IC1.17, IC2.17
  N18: IC1.18, IC2.18
  N19: IC1.19, IC2.19
  N20: IC1.20, IC2.20
  N21: IC1.21, IC2.21
  N22: IC1.22, IC2.22
  N23: IC1.23, IC2.23
  N24: IC1.24, IC2.24
  N25: IC1.25, IC2.25
  N26: IC1.26, IC2.26
  N27: IC1.27, IC2.27
  N28: IC1.28, IC2.28
