# Fritzing sketch microboard_pic16f (saved by Fritzing 0.8.3b)
circuit board: 3.92cm x 5cm
breadboards: 1

parts:
  GEN_SLOT = male pin header, 11 pins [form="♂ (male)"]
  SPI_SLOT = male pin header, 11 pins [form="♂ (male)"]
  IC2 = FTDI [package=SIL]
  PWR = male pin header, 2 pins [form="♂ (male)"]
  PSEL = male pin header, 3 pins [form="♂ (male)"]
  RESET = male pin header, 2 pins [form="♂ (male)"]
  PIC16F1827 = 16F1827 [package=DIL]
  R1 = Resistor [tolerance=±5% resistance=2.2k package=THT]
  R2 = Resistor [tolerance=±5% resistance=2.2k package=THT]

nets:
  GND: GEN_SLOT.pin1, SPI_SLOT.pin1, IC2.GND/Black, PWR.pin1, RESET.pin1, PIC16F1827.VSS
  VCC: GEN_SLOT.pin2, SPI_SLOT.pin2, PSEL.pin2, PIC16F1827.VDD, R1.Pin_0, R2.Pin_0
  N1: GEN_SLOT.pin4, PIC16F1827.RB1, R1.Pin_1
  N2: GEN_SLOT.pin5, PIC16F1827.RB4, R2.Pin_1
  N3: GEN_SLOT.pin7, PIC16F1827.RB0
  N4: GEN_SLOT.pin8, PIC16F1827.RA4
  N5: GEN_SLOT.pin10, PIC16F1827.RA2
  N6: GEN_SLOT.pin11, PIC16F1827.RA3
  N7: SPI_SLOT.pin3, PIC16F1827.RA1
  N8: SPI_SLOT.pin4, PIC16F1827.RA0
  N9: SPI_SLOT.pin5, PIC16F1827.RA7
  N10: SPI_SLOT.pin6, PIC16F1827.RA6
  N11: SPI_SLOT.pin8, PIC16F1827.RB7
  N12: SPI_SLOT.pin10, PIC16F1827.RB3
  N13: IC2.VCC, PSEL.pin1
  N14: IC2.TX, PIC16F1827.RB2
  N15: IC2.RX, PIC16F1827.RB5
  N16: PWR.pin2, PSEL.pin3
  RESET: RESET.pin2, PIC16F1827.RB6

notes:
  http://thegaragelab.com
  TGL Microboard
  +
  -
  Microboard MCU Prototyping Boards, Microboard PIC16F1827, 1C
