# Fritzing sketch powerboard (saved by Fritzing 0.8.7b)
circuit board: 8.5cm x 3.5cm
breadboards: 1

parts:
  IC3 = Voltage Regulator [package=to-220-alt]
  U1 = MCP1702 Voltage Regulator [part_number=3.3V package="TO92 [THT]"]
  C1 = Ceramic Capacitor [capacitance=100nF package="100 mil [THT, multilayer]"]
  C2 = Ceramic Capacitor [capacitance=100nF package="100 mil [THT, multilayer]"]
  R1 = Resistor [tolerance=±5% resistance=68 package=THT]
  R2 = Resistor [tolerance=±5% resistance=150 package=THT]
  LED1 = LED - 5mm [color="Red (633nm)" package="5 mm [THT]"]
  LED2 = LED - 5mm [color="Red (633nm)" package="5 mm [THT]"]
  PWR = female pin header, 2 pins [form="♀ (female)"]
  V33 = female pin header, 2 pins [form="♀ (female)"]
  V50 = female pin header, 2 pins [form="♀ (female)"]
  IC4 = TOGGLE [package=TSW]
  IC5 = TOGGLE [package=TSW]

nets:
  GND: IC3.GND, U1.GND, C1.0, C2.1, LED1.cathode, LED2.cathode, PWR.pin1, V33.pin2, V50.pin2
  N1: IC3.IN, IC5.UP1
  N2: IC3.OUT, R2.Pin_0, V50.pin1
  N3: U1.Vin, C1.1, IC4.UP1
  N4: U1.Vout, C2.0, R1.Pin_0, V33.pin1
  N5: R1.Pin_1, LED1.anode
  N6: R2.Pin_1, LED2.anode
  N7: PWR.pin2, IC4.IN1, IC5.IN1

notes:
  +VE
  3.3V
  5.0V

custom parts:
  MCP1702 Voltage Regulator: A MCP1702 Low Dropout Fixed Voltage Regulator (available in 1.2V, 1.5V, 1.8V, 2.5V, 2.8V, 3.0V, 3.3V, 4.0V, 5.0V)
