# Fritzing sketch microboard_lpc1114 (saved by Fritzing 0.8.3b)
circuit board: 3.92cm x 5cm
breadboards: 1

parts:
  GEN_SLOT = male pin header, 11 pins [form="♂ (male)"]
  SPI_SLOT = male pin header, 11 pins [form="♂ (male)"]
  IC2 = FTDI [package=SIL]
  PWR = male pin header, 2 pins [form="♂ (male)"]
  PSEL = male pin header, 3 pins [form="♂ (male)"]
  RESET = male pin header, 2 pins [form="♂ (male)"]
  R1 = Resistor [tolerance=±5% resistance=10k package=THT]
  LPC1114 = LPC1114 [package=DIL]
  R2 = Resistor [tolerance=±5% resistance=2.2k package=THT]
  R3 = Resistor [tolerance=±5% resistance=2.2k package=THT]

nets:
  GND: GEN_SLOT.pin1, SPI_SLOT.pin1, IC2.GND/Black, PWR.pin1, RESET.pin1, LPC1114.GNDA, LPC1114.GND
  VCC: GEN_SLOT.pin2, SPI_SLOT.pin2, PSEL.pin2, R1.Pin_0, LPC1114.VCCA, LPC1114.VCC, R2.Pin_0, R3.Pin_0
  N1: GEN_SLOT.pin3, LPC1114.D1_4/AD5
  N2: GEN_SLOT.pin4, LPC1114.D0_5/SDA, R3.Pin_1
  N3: GEN_SLOT.pin5, LPC1114.D0_4/SCL, R2.Pin_1
  N4: GEN_SLOT.pin6, LPC1114.D1_3/AD4
  N5: GEN_SLOT.pin7, LPC1114.D1_2/AD3
  N6: GEN_SLOT.pin8, LPC1114.D1_1/AD2
  N7: GEN_SLOT.pin9, LPC1114.D1_0/AD1
  N8: GEN_SLOT.pin10, LPC1114.D0_6
  N9: GEN_SLOT.pin11, LPC1114.D0_11/AD0
  N10: SPI_SLOT.pin3, LPC1114.D0_10
  N11: SPI_SLOT.pin4, LPC1114.D0_9/MOSI
  N12: SPI_SLOT.pin5, LPC1114.D0_8/MISO
  N13: SPI_SLOT.pin6, LPC1114.D0_7
  N14: SPI_SLOT.pin7, LPC1114.D0_3
  N15: SPI_SLOT.pin8, LPC1114.D0_2
  N16: SPI_SLOT.pin9, LPC1114.D1_9
  N17: SPI_SLOT.pin10, LPC1114.D1_8
  N18: SPI_SLOT.pin11, LPC1114.D1_5
  N19: IC2.VCC, PSEL.pin1
  N20: IC2.TX, LPC1114.D1_6/RXD
  N21: IC2.RX, LPC1114.D1_7/TXD
  N22: PWR.pin2, PSEL.pin3
  RESET: RESET.pin2, R1.Pin_1, LPC1114.D0_1

notes:
  http://thegaragelab.com
  TGL Microboard
  +
  -
  Microboard MCU Prototyping Boards, LPC1114 Microboard, 1B
