# Fritzing sketch microboard_pic16f (saved by Fritzing 0.8.3b)
circuit board: 3.92cm x 5cm
breadboards: 1

parts:
  GEN_SLOT = male pin header, 11 pins [form="♂ (male)"]
  SPI_SLOT = male pin header, 11 pins [form="♂ (male)"]
  IC2 = FTDI [package=SIL]
  PWR = male pin header, 2 pins [form="♂ (male)"]
  PSEL = male pin header, 3 pins [form="♂ (male)"]
  RESET = male pin header, 2 pins [form="♂ (male)"]
  R1 = Resistor [tolerance=±5% resistance=10k package=THT]
  PIC16F1827 = 16F1827 [package=DIL]

nets:
  GND: GEN_SLOT.pin1, SPI_SLOT.pin1, IC2.GND/Black, PWR.pin1, RESET.pin1, PIC16F1827.VSS
  VCC: GEN_SLOT.pin2, SPI_SLOT.pin2, PSEL.pin2, R1.Pin_0, PIC16F1827.VDD
  N1: GEN_SLOT.pin4, PIC16F1827.RB1
  N2: GEN_SLOT.pin5, PIC16F1827.RB4
  N3: GEN_SLOT.pin6, PIC16F1827.RA5
  N4: GEN_SLOT.pin7, PIC16F1827.RB0
  N5: GEN_SLOT.pin8, PIC16F1827.RA1
  N6: GEN_SLOT.pin9, PIC16F1827.RA4
  N7: GEN_SLOT.pin10, PIC16F1827.RA2
  N8: GEN_SLOT.pin11, PIC16F1827.RA3
  N9: SPI_SLOT.pin3, PIC16F1827.RA0
  N10: SPI_SLOT.pin4, PIC16F1827.RA7
  N11: SPI_SLOT.pin5, PIC16F1827.RA6
  N12: SPI_SLOT.pin6, PIC16F1827.RB7
  N13: SPI_SLOT.pin8, PIC16F1827.RB6
  N14: SPI_SLOT.pin10, PIC16F1827.RB3
  N15: IC2.VCC, PSEL.pin1
  N16: IC2.TX, PIC16F1827.RB2
  N17: IC2.RX, PIC16F1827.RB5
  N18: PWR.pin2, PSEL.pin3
  RESET: RESET.pin2, R1.Pin_1

notes:
  http://thegaragelab.com
  TGL Microboard
  +
  -
  Microboard MCU Prototyping Boards, Microboard PIC16F1827, 1A
