# Fritzing sketch microboard_pic32 (saved by Fritzing 0.8.3b)
circuit board: 3.92cm x 5cm
breadboards: 1

parts:
  GEN_SLOT = male pin header, 11 pins [form="♂ (male)"]
  SPI_SLOT = male pin header, 11 pins [form="♂ (male)"]
  IC2 = FTDI [package=SIL]
  PWR = male pin header, 2 pins [form="♂ (male)"]
  PSEL = male pin header, 3 pins [form="♂ (male)"]
  RESET = male pin header, 2 pins [form="♂ (male)"]
  R1 = Resistor [tolerance=±5% resistance=10k package=THT]
  PIC32MX = PIC32MX250F128 [package=DIL]
  R2 = Resistor [tolerance=±5% resistance=10k package=THT]
  R3 = Resistor [tolerance=±5% resistance=2.2k package=THT]
  R4 = Resistor [tolerance=±5% resistance=2.2k package=THT]

nets:
  GND: GEN_SLOT.pin1, SPI_SLOT.pin1, IC2.GND/Black, PWR.pin1, RESET.pin1, PIC32MX.Vss, PIC32MX.AVss
  VCC: GEN_SLOT.pin2, SPI_SLOT.pin2, PSEL.pin2, R1.Pin_0, PIC32MX.Vdd, PIC32MX.AVdd, R2.Pin_1, R3.Pin_0, R4.Pin_0
  N1: GEN_SLOT.pin4, PIC32MX.RB2, R3.Pin_1
  N2: GEN_SLOT.pin5, PIC32MX.RB3, R4.Pin_1
  N3: GEN_SLOT.pin6, PIC32MX.RA3
  N4: GEN_SLOT.pin7, PIC32MX.RA2
  N5: GEN_SLOT.pin8, PIC32MX.RB1
  N6: GEN_SLOT.pin9, PIC32MX.RB0
  N7: GEN_SLOT.pin10, PIC32MX.RA1
  N8: GEN_SLOT.pin11, PIC32MX.RA0
  N9: SPI_SLOT.pin3, PIC32MX.RB14
  N10: SPI_SLOT.pin4, PIC32MX.RB13
  N11: SPI_SLOT.pin5, PIC32MX.RB11
  N12: SPI_SLOT.pin6, PIC32MX.RB15
  N13: SPI_SLOT.pin7, PIC32MX.RB10
  N14: SPI_SLOT.pin8, PIC32MX.RB9
  N15: SPI_SLOT.pin9, PIC32MX.RB8
  N16: SPI_SLOT.pin10, PIC32MX.RB7
  N17: IC2.VCC, PSEL.pin1
  N18: IC2.TX, PIC32MX.RA4
  N19: IC2.RX, PIC32MX.RB4
  N20: PWR.pin2, PSEL.pin3
  RESET: RESET.pin2, R1.Pin_1, PIC32MX.RB5
  N21: PIC32MX.MCLR, R2.Pin_0

notes:
  http://thegaragelab.com
  TGL Microboard
  +
  -
  Microboard MCU Prototyping Boards, Microboard Template, 1B
