# Fritzing sketch microboard (saved by Fritzing 0.8.3b)
circuit board: 3.92cm x 5cm
breadboards: 1

parts:
  GEN_SLOT = male pin header, 11 pins [form="♂ (male)"]
  SPI_SLOT = male pin header, 11 pins [form="♂ (male)"]
  IC2 = FTDI [package=SIL]
  PWR = male pin header, 2 pins [form="♂ (male)"]
  PSEL = male pin header, 3 pins [form="♂ (male)"]
  RESET = male pin header, 2 pins [form="♂ (male)"]
  R1 = Resistor [tolerance=±5% resistance=10k package=THT]

nets:
  GND: GEN_SLOT.pin1, SPI_SLOT.pin1, IC2.GND/Black, PWR.pin1, RESET.pin1
  VCC: GEN_SLOT.pin2, SPI_SLOT.pin2, PSEL.pin2, R1.Pin_0
  N1: IC2.VCC, PSEL.pin1
  N2: PWR.pin2, PSEL.pin3
  RESET: RESET.pin2, R1.Pin_1

notes:
  http://thegaragelab.com
  TGL Microboard
  +
  -
  Microboard MCU Prototyping Boards, Microboard Template, 1A
